# Fritzing sketch Calculadora (saved by Fritzing 0.9.2b)
breadboards: 1

parts:
  Componente2 = Arduino Uno (Rev3)
  Componente3 = DeuLigne 1.1 - The Snootlab's LCD shield for Arduino
  S1 = Pushbutton [package="[THT]"]
  S2 = Pushbutton [package="[THT]"]
  S3 = Pushbutton [package="[THT]"]
  R1 = Resistor [tolerance=±5% resistance=1k package=THT]
  R2 = Resistor [tolerance=±5% resistance=1k package=THT]
  R3 = Resistor [tolerance=±5% resistance=1k package=THT]
  S4 = Pushbutton [package="[THT]"]
  R4 = Resistor [tolerance=±5% resistance=1k package=THT]
  S5 = Pushbutton [package="[THT]"]
  R5 = Resistor [tolerance=±5% resistance=1k package=THT]
  S6 = Pushbutton [package="[THT]"]
  R6 = Resistor [tolerance=±5% resistance=1k package=THT]
  S7 = Pushbutton [package="[THT]"]
  R7 = Resistor [tolerance=±5% resistance=1k package=THT]
  S8 = Pushbutton [package="[THT]"]
  R8 = Resistor [tolerance=±5% resistance=1k package=THT]
  S9 = Pushbutton [package="[THT]"]
  R9 = Resistor [tolerance=±5% resistance=1k package=THT]
  S0 = Pushbutton [package="[THT]"]
  R10 = Resistor [tolerance=±5% resistance=1k package=THT]
  EQ = Pushbutton [package="[THT]"]
  OP = Pushbutton [package="[THT]"]
  R11 = Resistor [tolerance=±5% resistance=1k package=THT]
  R12 = Resistor [tolerance=±5% resistance=1k package=THT]

nets:
  N1: Componente2.A0, Componente3.A0
  N2: Componente2.A1, Componente3.A1, R9.Pin_1, S0.Pin_1, R10.Pin_0
  N3: Componente2.A2, Componente3.A2
  N4: Componente2.A3, Componente3.A3
  N5: Componente2.A4/SDA, Componente3.A4(SDA)
  N6: Componente2.A5/SCL, Componente3.A5(CLK), EQ.Pin_4, R11.Pin_1, R12.Pin_0
  N7: Componente2.D8, Componente3.D8
  N8: Componente2.D9_PWM, Componente3.D9
  N9: Componente2.D10_PWM/SS, Componente3.D10_SS
  N10: Componente2.D11_PWM/MOSI, Componente3.D11_MOSI
  N11: Componente2.D12/MISO, Componente3.D12_MISO
  N12: Componente2.D13/SCK, Componente3.D13_SCK
  N13: Componente2.AREF, Componente3.AREF
  N14: Componente2.D0/RX, Componente3.D0_RX
  N15: Componente2.D1/TX, Componente3.D1_TX
  N16: Componente2.D2, Componente3.D2
  N17: Componente2.D3_PWM, Componente3.D3
  N18: Componente2.D4, Componente3.D4
  N19: Componente2.D5_PWM, Componente3.D5
  N20: Componente2.D6_PWM, Componente3.D6
  N21: Componente2.D7, Componente3.D7
  N22: Componente2.RESET, Componente3.RESET
  3V3: Componente2.3V3, Componente3.+3V3
  5V: Componente2.5V, Componente3.+5V, S1.Pin_3, S1.Pin_4, S2.Pin_3, S3.Pin_3, S4.Pin_3, S5.Pin_3, S6.Pin_3, S7.Pin_3, S7.Pin_4, S8.Pin_3, S8.Pin_4, S9.Pin_3, S9.Pin_4, S0.Pin_3, EQ.Pin_2, OP.Pin_1, OP.Pin_2
  GND: Componente2.GND, Componente3.GND, R10.Pin_1, R12.Pin_1
  VIN: Componente2.VIN, Componente3.VIN
  N23: S1.Pin_1, S1.Pin_2, R1.Pin_0
  N24: S2.Pin_1, S2.Pin_2, R1.Pin_1, R2.Pin_0
  N25: S3.Pin_1, S3.Pin_2, R2.Pin_1, R3.Pin_0
  N26: R3.Pin_1, S4.Pin_1, S4.Pin_2, R4.Pin_0
  N27: R4.Pin_1, S5.Pin_1, S5.Pin_2, R5.Pin_0
  N28: R5.Pin_1, S6.Pin_1, S6.Pin_2, R6.Pin_0
  N29: R6.Pin_1, S7.Pin_1, S7.Pin_2, R7.Pin_0
  N30: R7.Pin_1, S8.Pin_1, R8.Pin_0
  N31: R8.Pin_1, S9.Pin_1, R9.Pin_0
  N32: OP.Pin_4, R11.Pin_0
